# Fritzing sketch 12_RGB_LED_Ring_Clock (saved by Fritzing 0.9.3b)

parts:
  U1 = ESP32-38PinWide [part_number=ESP32-38PinWide]
  Part1 = 12 NeoPixel Ring [part_number=1643]
  J1 = female pin header, 1 pin [form="♀ (female)"]

nets:
  N1: U1.GPIO14, J1.pin1
  N2: U1.GPIO12, Part1.IN
  GND: U1.GND, Part1.GND
  VIN: U1.VIN, Part1.VDD

custom parts:
  ESP32-38PinWide: Generic 38-Pin ESP32 with wide format (only access to one side of pins on a breadboard) based on Stephen Lilley's HiLetgo ESP-WROOM-32 ESP32 ESP-32S Development Board.
  12 NeoPixel Ring: 12 ultra bright smart LED NeoPixels are arranged in a circle with 1.5" (37mm) outer diameter. The rings are 'chainable' - connect the output pin of one to the input pin of another. Use only one microcontroller pin to control as many as you can chain together! Each LED is addressable as the driver chip is inside the LED. Each one has ~18mA constant current drive so the color will be very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
